# Fritzing sketch fish (saved by Fritzing 0.9.5d)
breadboards: 1

parts:
  Mod1 = Raspberry Pi 4B  # not connected
  Componente1 = Arduino Mega 2560 (Rev3)
  HC-SR04_Sensor_1 = HC-SR04 Ultrasonic Distance Sensor
  HC-SR04_Sensor_2 = HC-SR04 Ultrasonic Distance Sensor
  HC-SR04_Sensor_3 = HC-SR04 Ultrasonic Distance Sensor
  HC-SR04_Sensor_4 = HC-SR04 Ultrasonic Distance Sensor
  HC-SR04_Sensor_5 = HC-SR04 Ultrasonic Distance Sensor
  HC-SR04_Sensor_6 = HC-SR04 Ultrasonic Distance Sensor
  HC-SR04_Sensor_7 = HC-SR04 Ultrasonic Distance Sensor
  HC-SR04_Sensor_8 = HC-SR04 Ultrasonic Distance Sensor
  USBTTL1 = USB A Plug
  USBTTL2 = Micro USB B Plug
  M2 = DC Motor
  M5 = DC Motor
  M6 = DC Motor
  M7 = DC Motor
  A1 = L298N DC motor driver
  A2 = L298N DC motor driver  # not connected
  BAT1 = Lithium Ion Polymer Battery 11.1v 5000mah
  BAT2 = 3-USB-Power-Bank-Battery-Pack  # not connected
  USBTTL3 = USB A Plug
  USBTTL4 = Micro USB B Plug
  S2 = Toggle Switch [package=THT]
  IC1 = Rasberry Pi NIOR Camera [chip_label=IC package="DIP (Dual Inline) [THT]"]  # not connected

nets:
  GND: Componente1.GND, HC-SR04_Sensor_1.GND, HC-SR04_Sensor_2.GND, HC-SR04_Sensor_3.GND, HC-SR04_Sensor_4.GND, HC-SR04_Sensor_5.GND, HC-SR04_Sensor_6.GND, HC-SR04_Sensor_7.GND, HC-SR04_Sensor_8.GND
  VCC: Componente1.5V, Componente1.D48, HC-SR04_Sensor_1.VCC, HC-SR04_Sensor_2.VCC, HC-SR04_Sensor_3.VCC, HC-SR04_Sensor_4.VCC, HC-SR04_Sensor_4.TRIG, HC-SR04_Sensor_5.VCC, HC-SR04_Sensor_6.VCC, HC-SR04_Sensor_7.VCC, HC-SR04_Sensor_8.VCC
  N1: Componente1.D24, HC-SR04_Sensor_3.TRIG
  N2: Componente1.D25, HC-SR04_Sensor_3.ECHO
  N3: Componente1.D28, HC-SR04_Sensor_8.TRIG
  N4: Componente1.D29, HC-SR04_Sensor_8.ECHO
  N5: Componente1.D32, HC-SR04_Sensor_5.TRIG
  N6: Componente1.D33, HC-SR04_Sensor_5.ECHO
  N7: Componente1.D36, HC-SR04_Sensor_6.TRIG
  N8: Componente1.D37, HC-SR04_Sensor_6.ECHO
  N9: Componente1.D40, HC-SR04_Sensor_7.TRIG
  N10: Componente1.D41, HC-SR04_Sensor_7.ECHO
  N11: Componente1.D44, HC-SR04_Sensor_2.TRIG
  N12: Componente1.D45, HC-SR04_Sensor_2.ECHO
  N13: Componente1.D49, HC-SR04_Sensor_4.ECHO
  N14: Componente1.D52, HC-SR04_Sensor_1.TRIG
  N15: Componente1.D53, HC-SR04_Sensor_1.ECHO
  N16: USBTTL1.usb, USBTTL2.usb
  N17: M2.pin_1, M6.pin_2
  N18: M2.pin_2, A1.OUT1
  N19: M5.pin_1, M7.pin_2
  N20: M5.pin_2, A1.OUT3
  N21: M6.pin_1, A1.OUT2
  N22: M7.pin_1, A1.OUT4
  N23: A1.12V, A1.5V-ENA-JMP-O, S2.COM
  N24: A1.GND, BAT1.negative
  N25: BAT1.positive, S2.L1
  N26: USBTTL3.usb, USBTTL4.usb

notes:
  Front

custom parts:
  L298N DC motor driver: This L298N Motor Driver Module is a high power motor driver module for driving DC and Stepper Motors. This module consists of an L298 motor driver IC and a 78M05 5V regulator.
  3-USB-Power-Bank-Battery-Pack: INIU B61 Power Bank 10000mAh, 3-Port Design.
  Rasberry Pi NIOR Camera: Camera
